# Fritzing sketch Esquema_projeto_fritzing (saved by Fritzing 0.8.7b)

parts:
  Componente1 = Arduino Uno (Rev3)
  Storage_microSD = OpenLog
  Acelerômetro = Triple Axis Gyro Breakout ITG-3200

nets:
  N1: Componente1.A4/SDA, Acelerômetro.SDA
  N2: Componente1.A5/SCL, Acelerômetro.SCL
  N3: Componente1.D11_PWM/MOSI, Storage_microSD.MOSI
  N4: Componente1.D12/MISO, Storage_microSD.MISO
  N5: Componente1.D13/SCK, Storage_microSD.SCK
  N6: Componente1.D4, Storage_microSD.RST
  VCC: Componente1.5V, Storage_microSD.VCC, Acelerômetro.VCC
  GND: Componente1.GND, Storage_microSD.GND, Acelerômetro.GND
